# Fritzing sketch Untitled Sketch (saved by Fritzing 0.9.3b)

parts:
  Part1 = Arduino Pro Mini v13
  R2 = Resistor [tolerance=±5% resistance=10k package="2512 [SMD]"]
  R3 = Resistor [tolerance=±5% resistance=10k package="2512 [SMD]"]
  R4 = Resistor [tolerance=±5% resistance=10k package="2512 [SMD]"]
  R5 = Resistor [tolerance=±5% resistance=10k package="2512 [SMD]"]
  Mod1 = KY-019 5V Relay Module [package="Breakout board"]
  OLED1 = OLED 128x64 I2C Monochrome Display GND-VDD
  R6 = Resistor [tolerance=±5% resistance=10k package="2512 [SMD]"]
  Power_plug1 = Power plug
  M1 = DC Motor
  Part2 = SO-24x [chip_label=SO-24x package=SO(x)]  # not connected

nets:
  GND: Part1.GND, Mod1.-, OLED1.GND, R6.Pin_1
  VCC: Part1.VCC, Mod1.+, OLED1.VDD
  N1: Part1.A3, R2.Pin_0
  N2: Part1.A2, R3.Pin_0
  N3: Part1.A1, R4.Pin_0
  N4: Part1.A0, R5.Pin_0
  N5: Part1.D10_PWM/SS, R6.Pin_0
  N6: Part1.D6_PWM, Mod1.S
  N7: Part1.D3_PWM, OLED1.SCK
  N8: Part1.D2, OLED1.SDA
  N9: Mod1.NC, M1.pin_1
  N10: Mod1.Common, Power_plug1.VCC

notes:
  Water Motor
  Power Supply
  Relay Module
  OLED Diplay
  Arduino Pro Micro
  10K
  5V
  20%
  60%
  80%
  100%
  40%
  0%
  Water Level

custom parts:
  KY-019 5V Relay Module: KY-019 5V Relay module, used to control AC circuits. (Special thanks to vanepp for fixing the PCB holes and other errors)
  OLED 128x64 I2C Monochrome Display GND-VDD: OLED 128x64 I2C Monochrome Display. Note: there are two variants of this part, this one is the GND VDD SCK SDA variant. The other is VDD GND SCK SDA. Make sure you select the part that matches your module as using the incorrect part will probably destroy your module! In addition the mounting holes are marked on silkscreen but not by default drilled. If you want drilled mounting holes, copy a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
